# Fritzing sketch Arduino-AVR-Switching-2 (saved by Fritzing 0.9.3b)
breadboards: 1

parts:
  Bauteil1 = Arduino Mega ADK (Rev3)
  LED1 = LED - 5mm [color="Red (633nm)" package="5 mm [THT]"]
  R1 = Resistor [tolerance=±5% resistance=220 package=THT]
  S1 = Pushbutton [package="[THT]"]
  R2 = Resistor [tolerance=±5% resistance=10k package=THT]

nets:
  N1: Bauteil1.5V, S1.Pin_3, S1.Pin_4
  N2: Bauteil1.GND, LED1.cathode, R2.Pin_1
  N3: Bauteil1.D48, R1.Pin_1
  N4: Bauteil1.D49, S1.Pin_1, S1.Pin_2, R2.Pin_0
  N5: LED1.anode, R1.Pin_0
