# Fritzing sketch Arduino-AVR-Switching (saved by Fritzing 0.9.3b)
breadboards: 1

parts:
  R1 = Resistor [tolerance=±5% resistance=220 package=THT]
  LED1 = LED - 5mm [color="Green (560nm)" package="5 mm [THT]"]
  R2 = Resistor [tolerance=±5% resistance=10k package=THT]
  S1 = Pushbutton [package="[THT]"]
  Bauteil1 = Arduino Ethernet Shield (Rev3)

nets:
  N1: R1.Pin_0, Bauteil1.PWM_D5
  N2: R1.Pin_1, LED1.anode
  N3: LED1.cathode, R2.Pin_0, Bauteil1.GND
  N4: R2.Pin_1, S1.Pin_3, S1.Pin_4, Bauteil1.SDCS
  N5: S1.Pin_1, S1.Pin_2, Bauteil1.5V
